// Logisim project Lab_5.circ as structural Verilog
module main (
);

  Accumulator_8Bit accumulator_8bit_1 ();  // open: Cin, A, Clk, S, Overflow
endmodule

module Ripple_Carry_Adder_4Bit (
  input  cin,
  input  [3:0] A,
  input  [3:0] B,
  output [3:0] S,
  output cout
);

  wire adder_1_cout, adder_2_cout, adder_3_cout;

  Adder #(.width(1)) adder_1 (.a(A[0]), .b(B[0]), .out(S[0]), .cin(cin), .cout(adder_1_cout));
  Adder #(.width(1)) adder_2 (.a(A[1]), .b(B[1]), .out(S[1]), .cin(adder_1_cout), .cout(adder_2_cout));
  Adder #(.width(1)) adder_3 (.a(A[2]), .b(B[2]), .out(S[2]), .cin(adder_2_cout), .cout(adder_3_cout));
  Adder #(.width(1)) adder_4 (.a(A[3]), .b(B[3]), .out(S[3]), .cin(adder_3_cout), .cout(cout));
endmodule

module Accumulator_8Bit (
  input  Cin,
  input  [7:0] A,
  input  Clk,
  output [7:0] S,
  output Overflow
);

  wire d_ff_1_qn, rca8_cout;
  wire [7:0] rca8_s, shift_register_1_out;

  Shift_Register #(.length(1), .parallel("false"), .width(8)) shift_register_1 (
    .shift(1'b1), .in(A), .clk(Clk), .out(shift_register_1_out), .clr(1'b0));  // open: load, d0, q0
  Ripple_Carry_Adder_8Bit rca8 (.Cin(Cin), .A(S), .B(shift_register_1_out), .S(rca8_s), .Cout(rca8_cout));
  Shift_Register #(.length(1), .parallel("false"), .width(8)) shift_register_2 (
    .shift(1'b1), .in(rca8_s), .clk(Clk), .out(S), .clr(1'b0));  // open: load, d0, q0
  D_Flip_Flop d_ff_1 (.D(rca8_cout), .clk(Clk), .Q(Overflow), .Qn(d_ff_1_qn), .preset(1'b0), .reset(1'b0));
  LED led_1 (.in(d_ff_1_qn));
endmodule

module Ripple_Carry_Adder_8Bit (
  input  Cin,
  input  [7:0] A,
  input  [7:0] B,
  output [7:0] S,
  output Cout
);

  wire ripple_carry_adder_4bit_1_cout;

  Ripple_Carry_Adder_4Bit ripple_carry_adder_4bit_1 (
    .cin(Cin), .A(A[3:0]), .B(B[3:0]), .S(S[3:0]), .cout(ripple_carry_adder_4bit_1_cout));
  Ripple_Carry_Adder_4Bit ripple_carry_adder_4bit_2 (
    .cin(ripple_carry_adder_4bit_1_cout), .A(A[7:4]), .B(B[7:4]), .S(S[7:4]), .cout(Cout));
endmodule

module Add_Sub_Accumulator (
  input  Sub,
  input  [7:0] A,
  input  Clk,
  output [7:0] S,
  output Overflow
);

  wire [7:0] xor_1_out;

  assign xor_1_out = {8{Sub}} ^ A;  // XOR_Gate xor_1, 8 bits wide
  Accumulator_8Bit Accu_8 (.Cin(Sub), .A(xor_1_out), .Clk(Clk), .S(S), .Overflow(Overflow));
endmodule

module Array_Multiplier_4Bit (
  input  [3:0] A,
  input  [3:0] B,
  output [7:0] P
);

  wire adder_1_cout, adder_2_cout, adder_2_out, adder_3_cout, adder_3_out, adder_4_cout, adder_4_out,
       adder_6_out, adder_7_out, adder_8_cout, adder_8_out, and_2_out, and_3_out, and_4_out, and_5_out,
       and_6_out, and_7_out, and_8_out, and_9_out, and_10_out, and_11_out, and_12_out, and_13_out,
       and_14_out, and_15_out, and_16_out;

  and and_1 (P[0], A[0], B[0]);
  and and_2 (and_2_out, A[1], B[0]);
  and and_3 (and_3_out, A[2], B[0]);
  and and_4 (and_4_out, A[3], B[0]);
  and and_5 (and_5_out, A[0], B[1]);
  and and_6 (and_6_out, A[1], B[1]);
  and and_7 (and_7_out, A[2], B[1]);
  and and_8 (and_8_out, A[3], B[1]);
  and and_9 (and_9_out, A[0], B[2]);
  and and_10 (and_10_out, A[1], B[2]);
  and and_11 (and_11_out, A[2], B[2]);
  and and_12 (and_12_out, A[3], B[2]);
  and and_13 (and_13_out, A[0], B[3]);
  and and_14 (and_14_out, A[1], B[3]);
  and and_15 (and_15_out, A[2], B[3]);
  and and_16 (and_16_out, A[3], B[3]);
  Adder #(.width(1)) adder_1 (.a(and_2_out), .b(and_5_out), .out(P[1]), .cin(1'b0), .cout(adder_1_cout));
  Adder #(.width(1)) adder_2 (.a(and_3_out), .b(and_6_out), .out(adder_2_out), .cin(adder_1_cout), .cout(adder_2_cout));
  Adder #(.width(1)) adder_3 (.a(and_4_out), .b(and_7_out), .out(adder_3_out), .cin(adder_2_cout), .cout(adder_3_cout));
  Adder #(.width(1)) adder_4 (.a(1'b0), .b(and_8_out), .out(adder_4_out), .cin(adder_3_cout), .cout(adder_4_cout));
  Adder #(.width(1)) adder_5 (.a(adder_2_out), .b(and_9_out), .out(P[2]), .cin(1'b0));  // open: cout
  Adder #(.width(1)) adder_6 (.a(adder_3_out), .b(and_10_out), .out(adder_6_out));  // open: cin, cout
  Adder #(.width(1)) adder_7 (.a(adder_4_out), .b(and_11_out), .out(adder_7_out));  // open: cin, cout
  Adder #(.width(1)) adder_8 (.a(adder_4_cout), .b(and_12_out), .out(adder_8_out), .cout(adder_8_cout));  // open: cin
  Adder #(.width(1)) adder_9 (.a(adder_6_out), .b(and_13_out), .out(P[3]), .cin(1'b0));  // open: cout
  Adder #(.width(1)) adder_10 (.a(adder_7_out), .b(and_14_out), .out(P[4]));  // open: cin, cout
  Adder #(.width(1)) adder_11 (.a(adder_8_out), .b(and_15_out), .out(P[5]));  // open: cin, cout
  Adder #(.width(1)) adder_12 (.a(adder_8_cout), .b(and_16_out), .out(P[6]), .cout(P[7]));  // open: cin
endmodule

module Array_Multiplier_8Bit (
  input  [7:0] A,
  input  [7:0] B,
  output [15:0] P
);

  wire [7:0] and_2_out, and_3_out, and_4_out, and_5_out, and_6_out, and_7_out, and_8_out;
  wire [7:1] and_1_out;

  assign {and_1_out, P[0]} = A & {8{B[0]}};  // AND_Gate and_1, 8 bits wide
  assign and_2_out = A & {8{B[1]}};  // AND_Gate and_2, 8 bits wide
  assign and_3_out = A & {8{B[2]}};  // AND_Gate and_3, 8 bits wide
  assign and_4_out = A & {8{B[3]}};  // AND_Gate and_4, 8 bits wide
  assign and_5_out = A & {8{B[4]}};  // AND_Gate and_5, 8 bits wide
  assign and_6_out = A & {8{B[5]}};  // AND_Gate and_6, 8 bits wide
  assign and_7_out = A & {8{B[6]}};  // AND_Gate and_7, 8 bits wide
  assign and_8_out = A & {8{B[7]}};  // AND_Gate and_8, 8 bits wide
  Ripple_Carry_Adder_8Bit ripple_carry_adder_8bit_1 ();  // open: Cin, A, B, S, Cout
  Ripple_Carry_Adder_8Bit ripple_carry_adder_8bit_2 ();  // open: Cin, A, B, S, Cout
  Ripple_Carry_Adder_8Bit ripple_carry_adder_8bit_3 ();  // open: Cin, A, B, S, Cout
  Ripple_Carry_Adder_8Bit ripple_carry_adder_8bit_4 ();  // open: Cin, A, B, S, Cout
  Ripple_Carry_Adder_8Bit ripple_carry_adder_8bit_5 ();  // open: Cin, A, B, S, Cout
  Ripple_Carry_Adder_8Bit ripple_carry_adder_8bit_6 ();  // open: Cin, A, B, S, Cout
  Ripple_Carry_Adder_8Bit ripple_carry_adder_8bit_7 ();  // open: Cin, A, B, S, Cout
endmodule
